// Logisim project cpu.circ as structural Verilog: 1 circuit, main circuit main
module main (
  input  CLK_RUN,
  input  CLK_HLT,
  input  [7:0] _8_Bit_Data_Bus,
  input  [15:0] in_4,
  input  in_5,
  input  in_6,
  input  IP_HI_TO_DATA,
  input  IP_LO_TO_DATA,
  input  DATA_TO_IP_HI,
  input  DATA_TO_IP_LO,
  input  IP_TO_ADDR,
  input  IP_INC,
  input  ADDR_TO_IP,
  input  DATA_TO_MAR_HI,
  input  DATA_TO_MAR_LO,
  input  MAR_INC,
  input  ADDR_TO_MAR,
  input  MDR_TO_DATA,
  input  DATA_TO_MDR,
  input  in_20,
  output [7:0] out_21,
  output [15:0] out_22,
  output [15:0] out_23,
  output [15:0] out_24,
  output [7:0] out_25
);

  wire and_1_out, and_2_out, CLK, CLK_STEP_out, clock_1_out, minus_CLK, nor_1_out, nor_2_out, nor_3_out,
       nor_4_out, not_1_out, not_2_out, not_3_out, or_1_out, or_2_out, or_3_out, RST;
  wire [7:0] controlled_buffer_3_out, controlled_buffer_4_out, controlled_buffer_9_out,
       controlled_buffer_11_out;

  Clock clock_1 (.out(clock_1_out));
  not not_1 (not_1_out, CLK_RUN);
  Button CLK_STEP (.out(CLK_STEP_out));
  Button u_RST (.out(RST));
  assign out_21 = in_5 ? _8_Bit_Data_Bus : 8'bz;  // Controlled_Buffer controlled_buffer_1
  and and_1 (and_1_out, clock_1_out, CLK_RUN);
  and and_2 (and_2_out, not_1_out, CLK_STEP_out);
  not not_2 (not_2_out, CLK_HLT);
  assign out_21 = IP_LO_TO_DATA ? out_23[7:0] : 8'bz;  // Controlled_Buffer controlled_buffer_2
  assign controlled_buffer_3_out = DATA_TO_IP_LO ? out_21 : 8'bz;  // Controlled_Buffer controlled_buffer_3
  assign controlled_buffer_4_out = DATA_TO_MAR_LO ? out_21 : 8'bz;  // Controlled_Buffer controlled_buffer_4
  assign out_25 = DATA_TO_MDR ? out_21 : 8'bz;  // Controlled_Buffer controlled_buffer_5
  assign out_21 = MDR_TO_DATA ? out_25 : 8'bz;  // Controlled_Buffer controlled_buffer_6
  or or_1 (or_1_out, and_1_out, and_2_out);
  and and_3 (CLK, or_1_out, not_2_out);
  assign out_21 = IP_HI_TO_DATA ? out_23[15:8] : 8'bz;  // Controlled_Buffer controlled_buffer_7
  nor nor_1 (nor_1_out, DATA_TO_IP_LO, ADDR_TO_IP);
  assign controlled_buffer_3_out = nor_1_out ? out_23[7:0] : 8'bz;  // Controlled_Buffer controlled_buffer_8
  assign controlled_buffer_9_out = DATA_TO_IP_HI ? out_21 : 8'bz;  // Controlled_Buffer controlled_buffer_9
  nor nor_2 (nor_2_out, DATA_TO_MAR_LO, ADDR_TO_MAR);
  assign controlled_buffer_4_out = nor_2_out ? out_24[7:0] : 8'bz;  // Controlled_Buffer controlled_buffer_10
  assign controlled_buffer_11_out = DATA_TO_MAR_HI ? out_21 : 8'bz;  // Controlled_Buffer controlled_buffer_11
  not not_3 (not_3_out, DATA_TO_MDR);
  not not_4 (minus_CLK, CLK);
  nor nor_3 (nor_3_out, DATA_TO_IP_HI, ADDR_TO_IP);
  assign controlled_buffer_9_out = nor_3_out ? out_23[15:8] : 8'bz;  // Controlled_Buffer controlled_buffer_12
  or or_2 (or_2_out, DATA_TO_IP_HI, DATA_TO_IP_LO, ADDR_TO_IP);
  nor nor_4 (nor_4_out, DATA_TO_MAR_HI, ADDR_TO_MAR);
  assign controlled_buffer_11_out = nor_4_out ? out_24[15:8] : 8'bz;  // Controlled_Buffer controlled_buffer_13
  or or_3 (or_3_out, DATA_TO_MAR_HI, DATA_TO_MAR_LO, ADDR_TO_MAR);
  Counter #(.width(16), .max('hffff)) IP (
    .load(or_2_out), .D({controlled_buffer_9_out, controlled_buffer_3_out}), .count(IP_INC), .Q(out_23),
    .clk(CLK), .clr(RST));  // open: carry
  Counter #(.width(16), .max('hffff)) MAR (
    .load(or_3_out), .D({controlled_buffer_11_out, controlled_buffer_4_out}), .count(MAR_INC), .Q(out_24),
    .clk(CLK));  // open: carry, clr
  RAM #(.addrWidth(16)) ram_1 (.addr(out_24), .data(out_25), .sel(1'b1), .clk(CLK), .ld(not_3_out));  // open: clr
  assign out_22 = in_6 ? in_4 : 16'bz;  // Controlled_Buffer controlled_buffer_14
  assign out_22 = IP_TO_ADDR ? out_23 : 16'bz;  // Controlled_Buffer controlled_buffer_15
  assign {controlled_buffer_9_out, controlled_buffer_3_out} = ADDR_TO_IP ? out_22 : 16'bz;  // Controlled_Buffer controlled_buffer_16
  assign {controlled_buffer_11_out, controlled_buffer_4_out} = ADDR_TO_MAR ? out_22 : 16'bz;  // Controlled_Buffer controlled_buffer_17

  // Notes on the sheet:
  //   Clock
  //   Instruction Pointer
  //   Memory Address Register
  //   Memory Data Register
  //   16-Bit Address Bus
endmodule
